// Digital circuit sumador_1bit.dig as structural Verilog
module sumador_1bit (
  input  A,
  input  B,
  input  Ci,
  output S,
  output Co
);

  wire semisumador_1bit_1_c0, semisumador_1bit_1_s, semisumador_1bit_2_c0;

  semisumador_1bit semisumador_1bit_1 (.A(A), .B(B), .S(semisumador_1bit_1_s), .C0(semisumador_1bit_1_c0));
  semisumador_1bit semisumador_1bit_2 (.A(semisumador_1bit_1_s), .B(Ci), .S(S), .C0(semisumador_1bit_2_c0));
  or or_1 (Co, semisumador_1bit_2_c0, semisumador_1bit_1_c0);
endmodule
