// Digital circuit sumador_4bits.dig as structural Verilog
module sumador_4bits (
  input  A0,
  input  A1,
  input  A2,
  input  A3,
  input  B0,
  input  B1,
  input  B2,
  input  B3,
  input  Ci,
  output S0,
  output S1,
  output S2,
  output S3,
  output Co
);

  wire sumador_1bit_1_co, sumador_1bit_2_co, sumador_1bit_3_co;

  sumador_1bit sumador_1bit_1 (.A(A0), .B(B0), .Ci(Ci), .S(S0), .Co(sumador_1bit_1_co));
  sumador_1bit sumador_1bit_2 (.A(A1), .B(B1), .Ci(sumador_1bit_1_co), .S(S1), .Co(sumador_1bit_2_co));
  sumador_1bit sumador_1bit_3 (.A(A2), .B(B2), .Ci(sumador_1bit_2_co), .S(S2), .Co(sumador_1bit_3_co));
  sumador_1bit sumador_1bit_4 (.A(A3), .B(B3), .Ci(sumador_1bit_3_co), .S(S3), .Co(Co));
endmodule
