// Digital circuit sumador_restador.dig as structural Verilog
module sumador_restador (
  input  A0,
  input  A1,
  input  A2,
  input  A3,
  input  B0,
  input  B1,
  input  B2,
  input  B3,
  input  selec,
  output S0,
  output S1,
  output S2,
  output S3,
  output S4
);

  wire xor_1_out, xor_2_out, xor_3_out, xor_4_out;

  xor xor_1 (xor_1_out, B0, selec);
  xor xor_2 (xor_2_out, B1, selec);
  xor xor_3 (xor_3_out, B2, selec);
  xor xor_4 (xor_4_out, B3, selec);
  sumador_4bits sumador_4bits_1 (
    .A0(A0), .A1(A1), .A2(A2), .A3(A3), .B0(xor_1_out), .B1(xor_2_out), .B2(xor_3_out), .B3(xor_4_out),
    .Ci(selec), .S0(S0), .S1(S1), .S2(S2), .S3(S3), .Co(S4));
endmodule
